# Fritzing sketch Etched-Glass-Plaque-Buttons (saved by Fritzing 0.9.2b)
circuit board: 3.58198cm x 1.04708cm
breadboards: 1

parts:
  JP1 = Header 3 [package=jst-3-pth]
  S1 = Pushbutton [package="[SMD]"]
  S2 = Pushbutton [package="[SMD]"]

nets:
  N1: JP1.1, S1.Pin_2, S2.Pin_1
  N2: JP1.2, S1.Pin_3, S1.Pin_4
  N3: JP1.3, S2.Pin_4

notes:
  BtN2
  BtN1
  GND
