# Fritzing sketch Etched-Glass-Plaque-MainBoard (saved by Fritzing 0.9.2b)
circuit board: 3.2cm x 3cm
breadboards: 1

parts:
  U1 = ATTINY45 [package=so]
  X1 = USB Connectors [package=usb-microb]
  JP2 = Header 6 [package=1x06-smd-female-v2]
  C2 = Capacitor Polarized [package=eia3216]
  usbasp = double row female pin header, 6 pins [form="♀ (female)"]

nets:
  N1: U1.PB5(NRES), usbasp.pin2
  GND: U1.GND, X1.GND, JP2.2, JP2.4, C2.-, usbasp.pin1
  N2: U1.PB0(MOSI), JP2.5, usbasp.pin5
  N3: U1.PB1(MISO), JP2.3, usbasp.pin4
  N4: U1.PB2(SCK_ADC1), JP2.1, usbasp.pin3
  N5: U1.VCC, X1.VBUS, JP2.6, C2.+, usbasp.pin6

notes:
  VCC
  DATA
  GND
  BtN1
  BtN2
  -----------
  MOSI
  MISO
  SCK
  RES
